// Logisim project Exercise_4.3_FlipFlop_RealChips.circ as structural Verilog: 1 circuit, main circuit main
module main (
  input  DataBit,
  input  WriteEnable,
  output DataOut
);

  wire n7400_1_pin3, n7400_1_pin6, n7400_1_pin9, n7400_1_pin11;

  _7400 #(.ShowInternalStructure("true")) u_7400_1 (
    .pin1(DataBit), .pin2(DataBit), .pin3(n7400_1_pin3), .pin4(n7400_1_pin3), .pin5(WriteEnable),
    .pin6(n7400_1_pin6), .pin13(WriteEnable), .pin12(DataBit), .pin11(n7400_1_pin11), .pin10(n7400_1_pin11),
    .pin9(n7400_1_pin9), .pin8(DataOut));
  // _7400 #(.ShowInternalStructure("true")) 7400_2: pin names not known; wires that end beside it: 1'b1, n7400_1_pin6, DataOut, n7400_1_pin9, 1'b0
endmodule
