// Logisim project Exercise_4_Logisim_Simulation.circ as structural Verilog: 1 circuit, main circuit main
module main (
  input  DataBit1,
  input  WriteEnable1,
  input  DataBit2,
  input  WriteEnable2,
  output DataOut1,
  output DataOut2
);

  wire and_1_out, and_2_out, nand_1_out, nand_2_out, nand_3_out, nand_5_out, not_1_out, not_2_out;

  not not_1 (not_1_out, DataBit1);
  not not_2 (not_2_out, DataBit2);
  nand nand_1 (nand_1_out, DataBit1, WriteEnable1);
  nand nand_2 (nand_2_out, WriteEnable1, not_1_out);
  and and_1 (and_1_out, DataBit2, WriteEnable2);
  nand nand_3 (nand_3_out, WriteEnable2, not_2_out);
  nand nand_4 (DataOut1, nand_1_out, nand_5_out);
  nand nand_5 (nand_5_out, DataOut1, nand_2_out);
  or or_1 (DataOut2, and_1_out, and_2_out);
  and and_2 (and_2_out, DataOut2, nand_3_out);
endmodule
